# Fritzing sketch Arduino (saved by Fritzing 0.9.4)
breadboards: 1

parts:
  パーツ1 = Adafruit INA219 [part_number="Adafruit #904"]
  パーツ2 = Arduino Uno (Rev3)
  J1 = screw terminal, 3 pins
  OLED_I2C1 = OLED 128x64 I2C Monochrome Display

nets:
  N1: パーツ1.SCL, パーツ2.A5/SCL, OLED_I2C1.SCL
  N2: パーツ1.VIN-, J1.pin1
  N3: パーツ1.VIN+, J1.pin2
  VCC: パーツ1.VCC, パーツ2.5V, OLED_I2C1.VDD
  GND: パーツ1.GND, パーツ2.GND, J1.pin3, OLED_I2C1.GND
  N4: パーツ1.SDA, パーツ2.A4/SDA, OLED_I2C1.SDA

custom parts:
  Adafruit INA219: This breakout board will solve all your power-monitoring problems. Instead of struggling with two multimeters, you can just use the handy INA219B chip on this breakout to both measure both the high side voltage and DC current draw over I2C with 1% precision. Most current-measuring devices such as our current panel meter are only good for low side measuring. That means that unless you want to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
